// Logisim project Project 1 - NAND.circ as structural Verilog: 1 circuit, main circuit main
module main (
  input  A,
  input  B,
  input  C
);

  wire nand_1_out, nand_2_out, nand_3_out, nand_4_out, nand_5_out, nand_6_out, not_1_out, not_2_out,
       not_3_out;

  not not_1 (not_1_out, B);
  not not_2 (not_2_out, A);
  not not_3 (not_3_out, C);
  nand nand_1 (nand_1_out, A, B, C);
  nand nand_2 (nand_2_out, not_2_out, B, C);
  nand nand_3 (nand_3_out, A, not_1_out, not_3_out);
  nand nand_4 (nand_4_out, A, not_1_out, C);
  nand nand_5 (nand_5_out, not_2_out, not_1_out, C);
  nand nand_6 (nand_6_out, nand_1_out, nand_2_out, nand_3_out, nand_4_out, nand_5_out);
  LED led_1 (.in(nand_6_out));

  // Notes on the sheet:
  //   f(A, B, C) = ABC + A'BC + AB'C' + AB'C + A'B'C
endmodule
